// Logisim project cpu.circ as structural Verilog: 20 circuits, main circuit main
// CPU
module main (
  input  [31:0] RS_READ_VALUE,
  input  [31:0] RI_READ_VALUE,
  input  [31:0] RD_READ_VALUE,
  input  [31:0] JC_READ_VALUE,
  input  [31:0] INSTRUCTION,
  input  CLOCK,
  output [4:0] RS,
  output [4:0] RI,
  output [4:0] RD,
  output [31:0] RD_WRITE_VALUE,
  output RD_WRITE_ENABLE,
  output [23:0] FETCH_ADDRESS
);

  wire JAL, jump, load, mem, mem_write, RI_or_addr, RI_or_imm, word_mode;
  wire [2:0] JC;
  wire [3:0] OP;
  wire [4:0] RD_bits;
  wire [23:0] bit_extender_1_out, fetch, inst_addr, jump_addr, PC_1;
  wire [24:0] bit_extender_3_out;
  wire [31:0] ALU_result, bit_extender_2_out, data_out, imm, multiplexer_1_out;

  Register #(.width(24)) PC (.D(fetch), .Q(FETCH_ADDRESS), .clk(CLOCK));  // open: en, clr
  u_DECODE DECODE (
    .instruction(INSTRUCTION), .RI_bits(RI), .RS_bits(RS), .RD_bits(RD_bits), .JC(JC), .OP(OP),
    .RI_or_imm(RI_or_imm), .RI_or_addr(RI_or_addr), .addr(inst_addr), .IMM(imm));
  Adder #(.width(24)) adder_1 (.a(FETCH_ADDRESS), .b(24'h1), .out(PC_1));  // open: cin, cout
  Multiplexer #(.width(32)) multiplexer_1 (
    .in0(RI_READ_VALUE), .in1(imm), .out(multiplexer_1_out), .sel(RI_or_imm));  // open: en
  Bit_Extender #(.in_width(32), .out_width(24)) bit_extender_1 (.in(RI_READ_VALUE), .out(bit_extender_1_out));
  u_ALU u_alu_1 (
    .RS_val(RS_READ_VALUE), .RI_val_or_immediate(multiplexer_1_out), .ALU_RESULT(ALU_result), .ALU_CONTROL(OP));
  assign bit_extender_2_out = {{8{1'b0}}, PC_1};  // Bit_Extender bit_extender_2
  // Probe on ALU_result
  u_CONTROL Control (
    .JC(JC), .OP(OP), .I_bit(RI_or_imm), .jc_value(JC_READ_VALUE), .jumping(jump),
    .RD_write(RD_WRITE_ENABLE), .mem(mem), .mem_write(mem_write), .word_mode(word_mode), .JAL(JAL),
    .load(load));
  Multiplexer #(.width(24)) multiplexer_2 (
    .in0(bit_extender_1_out), .in1(inst_addr), .out(jump_addr), .sel(RI_or_addr));  // open: en
  Multiplexer #(.select(2), .width(32)) multiplexer_3 (
    .in0(ALU_result), .in1(data_out), .in2(bit_extender_2_out), .out(RD_WRITE_VALUE), .sel({JAL, load}));  // open: in3, en
  Bit_Extender #(.in_width(32), .out_width(25)) bit_extender_3 (.in(ALU_result), .out(bit_extender_3_out));
  // Probe on {JAL, load}
  Multiplexer #(.width(5)) multiplexer_4 (.in0(RD_bits), .in1(5'b00110), .out(RD), .sel(JAL));  // open: en
  Multiplexer #(.width(24)) multiplexer_5 (.in0(PC_1), .in1(jump_addr), .out(fetch), .sel(jump));  // open: en
  u_MEM u_mem_1 (
    .ADDRESS(bit_extender_3_out), .WORD_MODE(word_mode), .MEM_WRITE(mem_write), .DATA_IN(RD_READ_VALUE),
    .CLOCK(CLOCK), .DATA_OUT(data_out), .ENABLE(mem), .load(load));

  // Other names for the same wires on the sheet: clk = CLOCK; JC_value[31:0] = JC_READ_VALUE;
  //   PC[23:0] = FETCH_ADDRESS; RD_value[31:0] = RD_READ_VALUE; rd_write_val[31:0] = RD_WRITE_VALUE;
  //   RI_bits[4:0] = RI; RI_value[31:0] = RI_READ_VALUE; RS_bits[4:0] = RS; RS_value[31:0] = RS_READ_VALUE

  // Notes on the sheet:
  //   these 3 go to regfile
  //   from control(?)
  //   from instruction memory
  //   from regfile
  //   from regfile
  //   from regfile
endmodule

module u_ALU (
  input  [31:0] RS_val,
  input  [31:0] RI_val_or_immediate,
  input  [3:0] ALU_CONTROL,
  output [31:0] ALU_RESULT
);

  wire [4:0] bit_extender_1_out, bit_extender_2_out, bit_extender_3_out;
  wire [31:0] add, \and , div, mul, \or , rev, sl, sr, stu, sub, \xor ;

  // Probe on RS_val
  // Probe on RI_val_or_immediate
  u_ALU_shiftLeft u_alu_shiftleft_1 (.\input (RS_val), .shift_amount(bit_extender_1_out), .\output (sl));
  Bit_Extender #(.in_width(32), .out_width(5)) bit_extender_1 (.in(RI_val_or_immediate), .out(bit_extender_1_out));
  Shifter #(.width(32), .shift("ar")) shifter_1 (.in(RS_val), .\dist (bit_extender_2_out), .out(sr));
  Bit_Extender #(.in_width(32), .out_width(5)) bit_extender_2 (.in(RI_val_or_immediate), .out(bit_extender_2_out));
  assign \and  = RS_val & RI_val_or_immediate;  // AND_Gate AND, 32 bits wide
  assign \or  = RS_val | RI_val_or_immediate;  // OR_Gate OR, 32 bits wide
  u_REV u_rev_1 (.INPUT(RS_val), .REVERSE_AMOUNT(bit_extender_3_out), .OUTPUT(rev));
  Bit_Extender #(.in_width(32), .out_width(5)) bit_extender_3 (.in(RI_val_or_immediate), .out(bit_extender_3_out));
  assign \xor  = RS_val ^ RI_val_or_immediate;  // XOR_Gate XOR, 32 bits wide
  Adder #(.width(32)) adder_1 (.a(RS_val), .b(RI_val_or_immediate), .out(add));  // open: cin, cout
  Subtractor #(.width(32)) subtractor_1 (.a(RS_val), .b(RI_val_or_immediate), .out(sub));  // open: bin, bout
  Multiplier #(.width(32)) multiplier_1 (.a(RS_val), .b(RI_val_or_immediate), .out(mul));  // open: cin, cout
  u_DIV u_div_1 (.rs_val(RS_val), .val_2(RI_val_or_immediate), .out(div));
  Bit_Extender #(.in_width(32), .out_width(15)) bit_extender_4 (.in(RS_val), .out(stu[14:0]));
  Bit_Extender #(.in_width(32), .out_width(17)) bit_extender_5 (.in(RI_val_or_immediate), .out(stu[31:15]));
  Multiplexer #(.select(4), .width(32)) multiplexer_1 (
    .in0(sl), .in1(sr), .in2(\and ), .in3(\or ), .in4(rev), .in5(\xor ), .in6(add), .in7(sub), .in8(mul),
    .in9(div), .in10(add), .in11(add), .in12(add), .in13(add), .in14(stu), .in15({32{1'b0}}),
    .out(ALU_RESULT), .sel(ALU_CONTROL));  // open: en
  // Probe on ALU_RESULT

  // Other names for the same wires on the sheet: pick[3:0] = ALU_CONTROL; RI_val_imm[31:0] = RI_val_or_immediate;
  //   lh[31:0] = add; lw[31:0] = add; sh[31:0] = add; sw[31:0] = add

  // Notes on the sheet:
  //   implement a diff divide
endmodule

// Data Memory
module u_MEM (
  input  [24:0] ADDRESS,
  input  WORD_MODE,
  input  MEM_WRITE,
  input  [31:0] DATA_IN,
  input  CLOCK,
  input  ENABLE,
  input  load,
  output [31:0] DATA_OUT
);

  wire and_1_out, and_2_out, and_3_out, and_4_out, bit_extender_1_out, even, odd, OR_4_out, OR_out;
  wire [15:0] even_half, even_out, multiplexer_3_out, multiplexer_4_out, odd_half, odd_out;
  wire [24:0] addr_1, addr_in, odd_in;
  wire [31:0] bit_extender_2_out, bit_extender_3_out, multiplexer_7_out, multiplexer_8_out, OR_2_out,
       OR_3_out, shifter_1_out, shifter_2_out;

  Demultiplexer demultiplexer_1 (.out0(even), .out1(odd), .in(ENABLE), .sel(bit_extender_1_out));  // open: en
  Bit_Extender #(.in_width(25), .out_width(1)) bit_extender_1 (.in(ADDRESS), .out(bit_extender_1_out));
  Multiplexer #(.width(25)) multiplexer_1 (.in0(ADDRESS), .in1(addr_1), .out(addr_in), .sel(odd));  // open: en
  Multiplexer #(.width(25)) multiplexer_2 (.in0(ADDRESS), .in1(addr_1), .out(odd_in), .sel(even));  // open: en
  and and_1 (and_1_out, odd, WORD_MODE);
  and and_2 (and_2_out, even, WORD_MODE);
  // Probe on even_half
  Multiplexer #(.width(16)) multiplexer_3 (
    .in0({16{1'b0}}), .in1(DATA_IN[31:16]), .out(multiplexer_3_out), .sel(and_1_out));  // open: en
  Multiplexer #(.width(16)) multiplexer_4 (
    .in0({16{1'b0}}), .in1(DATA_IN[31:16]), .out(multiplexer_4_out), .sel(and_2_out));  // open: en
  Multiplexer #(.width(16)) multiplexer_5 (
    .in0(multiplexer_3_out), .in1(DATA_IN[15:0]), .out(even_half), .sel(even));  // open: en
  // Probe on odd_half
  Multiplexer #(.width(16)) multiplexer_6 (
    .in0(multiplexer_4_out), .in1(DATA_IN[15:0]), .out(odd_half), .sel(odd));  // open: en
  // Probe on even_half
  or OR (OR_out, even, WORD_MODE);
  assign bit_extender_2_out = {{16{1'b0}}, even_out};  // Bit_Extender bit_extender_2
  assign bit_extender_3_out = {{16{1'b0}}, odd_out};  // Bit_Extender bit_extender_3
  RAM #(.addrWidth(24), .dataWidth(16), .bus("separate")) ram_1 (
    .addr(addr_in[24:1]), .din(even_half), .data(even_out), .str(OR_out), .clk(CLOCK), .ld(1'b1));  // open: sel, clr
  Multiplexer #(.width(32)) multiplexer_7 (
    .in0(bit_extender_2_out), .in1(bit_extender_3_out), .out(multiplexer_7_out), .sel(odd));  // open: en
  // Probe on nothing
  Multiplexer #(.width(32)) multiplexer_8 (
    .in0(multiplexer_7_out), .in1(OR_3_out), .out(multiplexer_8_out), .sel(and_3_out));  // open: en
  Shifter #(.width(32)) shifter_1 (.in(bit_extender_3_out), .\dist (5'b10000), .out(shifter_1_out));
  Shifter #(.width(32)) shifter_2 (.in(bit_extender_2_out), .\dist (5'b10000), .out(shifter_2_out));
  assign OR_2_out = shifter_2_out | bit_extender_3_out;  // OR_Gate OR_2, 32 bits wide
  // Probe on odd_half
  and and_3 (and_3_out, even, WORD_MODE);
  assign OR_3_out = shifter_1_out | bit_extender_2_out;  // OR_Gate OR_3, 32 bits wide
  or OR_4 (OR_4_out, odd, WORD_MODE);
  Adder #(.width(25)) adder_1 (.a(ADDRESS), .b(25'h1), .out(addr_1));  // open: cin, cout
  Multiplexer #(.width(32)) multiplexer_9 (
    .in0(multiplexer_8_out), .in1(OR_2_out), .out(DATA_OUT), .sel(and_4_out));  // open: en
  and and_4 (and_4_out, odd, WORD_MODE);
  RAM #(.addrWidth(24), .dataWidth(16), .bus("separate")) ram_2 (
    .addr(odd_in[24:1]), .din(odd_half), .data(odd_out), .str(OR_4_out), .clk(CLOCK), .ld(1'b1));  // open: sel, clr

  // Other names for the same wires on the sheet: addr[24:0] = ADDRESS; clk = CLOCK; even_input[15:0] = DATA_IN[15:0];
  //   lower_16[15:0] = DATA_IN[15:0]; odd_input[15:0] = DATA_IN[31:16]; upper_16[15:0] = DATA_IN[31:16];
  //   even_in[24:0] = addr_in; out[31:0] = DATA_OUT; use = ENABLE; word = WORD_MODE; write = MEM_WRITE

  // Notes on the sheet:
  //   shift odd input right when storing half
  //   shift even input left when storing half
  //   However, you *SHOULD* use 2 RAM modules, one for even addresses and one for odd addresses.
  //   You might use the word mode input to differentiate LW/SW from LH/SH.
  //   set word mode depending on word (1) or half-word (0)
  //   set mem_write depending on store (1) or load (0)
  //   even addr
  //   odd half will have upper 16 bits
  //   only use data out if loading
  //   odd addr
endmodule

module u_REV (
  input  [31:0] INPUT,
  input  [4:0] REVERSE_AMOUNT,
  output [31:0] OUTPUT
);

  wire [31:0] multiplexer_1_out, multiplexer_2_out, multiplexer_3_out, multiplexer_4_out, u_alu_rb1_1_out,
       u_alu_rb2_1_out, u_alu_rb4_1_out, u_alu_rb8_1_out, u_alu_rb16_1_out;

  u_ALU_rb16 u_alu_rb16_1 (.value(INPUT), .out(u_alu_rb16_1_out));
  Multiplexer #(.width(32)) multiplexer_1 (
    .in0(INPUT), .in1(u_alu_rb16_1_out), .out(multiplexer_1_out), .sel(REVERSE_AMOUNT[4]));  // open: en
  u_ALU_rb8 u_alu_rb8_1 (.value(multiplexer_1_out), .out(u_alu_rb8_1_out));
  Multiplexer #(.width(32)) multiplexer_2 (
    .in0(multiplexer_1_out), .in1(u_alu_rb8_1_out), .out(multiplexer_2_out), .sel(REVERSE_AMOUNT[3]));  // open: en
  u_ALU_rb4 u_alu_rb4_1 (.value(multiplexer_2_out), .out(u_alu_rb4_1_out));
  Multiplexer #(.width(32)) multiplexer_3 (
    .in0(multiplexer_2_out), .in1(u_alu_rb4_1_out), .out(multiplexer_3_out), .sel(REVERSE_AMOUNT[2]));  // open: en
  u_ALU_rb2 u_alu_rb2_1 (.value(multiplexer_3_out), .out(u_alu_rb2_1_out));
  Multiplexer #(.width(32)) multiplexer_4 (
    .in0(multiplexer_3_out), .in1(u_alu_rb2_1_out), .out(multiplexer_4_out), .sel(REVERSE_AMOUNT[1]));  // open: en
  u_ALU_rb1 u_alu_rb1_1 (.value(multiplexer_4_out), .out(u_alu_rb1_1_out));
  Multiplexer #(.width(32)) multiplexer_5 (
    .in0(multiplexer_4_out), .in1(u_alu_rb1_1_out), .out(OUTPUT), .sel(REVERSE_AMOUNT[0]));  // open: en

  // Other names for the same wires on the sheet: r1 = REVERSE_AMOUNT[0]; r2 = REVERSE_AMOUNT[1];
  //   r3 = REVERSE_AMOUNT[2]; r4 = REVERSE_AMOUNT[3]; r5 = REVERSE_AMOUNT[4]

  // Notes on the sheet:
  //   rb is reverse by!
endmodule

module u_ALU_shiftLeft (
  input  [31:0] \input ,
  input  [4:0] shift_amount,
  output [31:0] \output 
);

  wire [31:0] multiplexer_1_out, multiplexer_2_out, multiplexer_3_out, multiplexer_4_out, u_alu_sb1_1_out,
       u_alu_sb2_1_out, u_alu_sb4_1_out, u_alu_sb8_1_out, u_alu_sb16_1_out;

  u_ALU_sb1 u_alu_sb1_1 (.in(\input ), .out(u_alu_sb1_1_out));
  Multiplexer #(.width(32)) multiplexer_1 (
    .in0(\input ), .in1(u_alu_sb1_1_out), .out(multiplexer_1_out), .sel(shift_amount[0]));  // open: en
  Multiplexer #(.width(32)) multiplexer_2 (
    .in0(multiplexer_1_out), .in1(u_alu_sb2_1_out), .out(multiplexer_2_out), .sel(shift_amount[1]));  // open: en
  u_ALU_sb2 u_alu_sb2_1 (.in(multiplexer_1_out), .out(u_alu_sb2_1_out));
  u_ALU_sb4 u_alu_sb4_1 (.in(multiplexer_2_out), .out(u_alu_sb4_1_out));
  Multiplexer #(.width(32)) multiplexer_3 (
    .in0(multiplexer_2_out), .in1(u_alu_sb4_1_out), .out(multiplexer_3_out), .sel(shift_amount[2]));  // open: en
  Multiplexer #(.width(32)) multiplexer_4 (
    .in0(multiplexer_3_out), .in1(u_alu_sb8_1_out), .out(multiplexer_4_out), .sel(shift_amount[3]));  // open: en
  u_ALU_sb8 u_alu_sb8_1 (.in(multiplexer_3_out), .out(u_alu_sb8_1_out));
  u_ALU_sb16 u_alu_sb16_1 (.in(multiplexer_4_out), .out(u_alu_sb16_1_out));
  Multiplexer #(.width(32)) multiplexer_5 (
    .in0(multiplexer_4_out), .in1(u_alu_sb16_1_out), .out(\output ), .sel(shift_amount[4]));  // open: en

  // Other names for the same wires on the sheet: s1 = shift_amount[0]; s2 = shift_amount[1]; s3 = shift_amount[2];
  //   s4 = shift_amount[3]; s5 = shift_amount[4]

  // Notes on the sheet:
  //   sb is shift by, not store byte!
endmodule

module u_ALU_sb1 (
  input  [31:0] in,
  output [31:0] out
);

  wire bit_extender_1_out, bit_extender_3_out;
  wire [31:0] bit_extender_2_out, shifter_1_out;

  Bit_Extender #(.in_width(32), .out_width(1)) bit_extender_1 (.in(in), .out(bit_extender_1_out));
  Shifter #(.width(32)) shifter_1 (.in(in), .\dist (5'b00001), .out(shifter_1_out));
  assign bit_extender_2_out = {{31{1'b0}}, bit_extender_3_out};  // Bit_Extender bit_extender_2
  Bit_Extender #(.in_width(1), .out_width(1), .\type ("sign")) bit_extender_3 (
    .in(bit_extender_1_out), .out(bit_extender_3_out));
  assign out = shifter_1_out | bit_extender_2_out;  // OR_Gate OR, 32 bits wide
endmodule

module u_ALU_sb2 (
  input  [31:0] in,
  output [31:0] out
);

  wire bit_extender_1_out;
  wire [1:0] bit_extender_3_out;
  wire [31:0] bit_extender_2_out, shifter_1_out;

  Bit_Extender #(.in_width(32), .out_width(1)) bit_extender_1 (.in(in), .out(bit_extender_1_out));
  Shifter #(.width(32)) shifter_1 (.in(in), .\dist (5'b00010), .out(shifter_1_out));
  assign bit_extender_2_out = {{30{1'b0}}, bit_extender_3_out};  // Bit_Extender bit_extender_2
  assign bit_extender_3_out = {{1{bit_extender_1_out}}, bit_extender_1_out};  // Bit_Extender bit_extender_3
  assign out = shifter_1_out | bit_extender_2_out;  // OR_Gate OR, 32 bits wide
endmodule

module u_ALU_sb4 (
  input  [31:0] in,
  output [31:0] out
);

  wire bit_extender_1_out;
  wire [3:0] bit_extender_2_out;
  wire [31:0] bit_extender_3_out, shifter_1_out;

  Bit_Extender #(.in_width(32), .out_width(1)) bit_extender_1 (.in(in), .out(bit_extender_1_out));
  Shifter #(.width(32)) shifter_1 (.in(in), .\dist (5'b00100), .out(shifter_1_out));
  assign bit_extender_2_out = {{3{bit_extender_1_out}}, bit_extender_1_out};  // Bit_Extender bit_extender_2
  assign bit_extender_3_out = {{28{1'b0}}, bit_extender_2_out};  // Bit_Extender bit_extender_3
  assign out = shifter_1_out | bit_extender_3_out;  // OR_Gate OR, 32 bits wide
endmodule

module u_ALU_sb8 (
  input  [31:0] in,
  output [31:0] out
);

  wire bit_extender_1_out;
  wire [7:0] bit_extender_3_out;
  wire [31:0] bit_extender_2_out, shifter_1_out;

  Bit_Extender #(.in_width(32), .out_width(1)) bit_extender_1 (.in(in), .out(bit_extender_1_out));
  Shifter #(.width(32)) shifter_1 (.in(in), .\dist (5'b01000), .out(shifter_1_out));
  assign bit_extender_2_out = {{24{1'b0}}, bit_extender_3_out};  // Bit_Extender bit_extender_2
  assign bit_extender_3_out = {{7{bit_extender_1_out}}, bit_extender_1_out};  // Bit_Extender bit_extender_3
  assign out = shifter_1_out | bit_extender_2_out;  // OR_Gate OR, 32 bits wide
endmodule

module u_ALU_sb16 (
  input  [31:0] in,
  output [31:0] out
);

  wire bit_extender_1_out;
  wire [15:0] bit_extender_3_out;
  wire [31:0] bit_extender_2_out, shifter_1_out;

  Bit_Extender #(.in_width(32), .out_width(1)) bit_extender_1 (.in(in), .out(bit_extender_1_out));
  Shifter #(.width(32)) shifter_1 (.in(in), .\dist (5'b10000), .out(shifter_1_out));
  assign bit_extender_2_out = {{16{1'b0}}, bit_extender_3_out};  // Bit_Extender bit_extender_2
  assign bit_extender_3_out = {{15{bit_extender_1_out}}, bit_extender_1_out};  // Bit_Extender bit_extender_3
  assign out = shifter_1_out | bit_extender_2_out;  // OR_Gate OR, 32 bits wide
endmodule

module u_ALU_rb1 (
  input  [31:0] value,
  output [31:0] out
);


  assign out = {value[30], value[31], value[28], value[29], value[26], value[27], value[24], value[25], value[22], value[23], value[20], value[21], value[18], value[19], value[16], value[17], value[14], value[15], value[12], value[13], value[10], value[11], value[8], value[9], value[6], value[7], value[4], value[5], value[2], value[3], value[0], value[1]};
endmodule

module u_ALU_rb2 (
  input  [31:0] value,
  output [31:0] out
);


  assign out = {value[29:28], value[31:30], value[25:24], value[27:26], value[21:20], value[23:22], value[17:16], value[19:18], value[13:12], value[15:14], value[9:8], value[11:10], value[5:4], value[7:6], value[1:0], value[3:2]};
endmodule

module u_ALU_rb4 (
  input  [31:0] value,
  output [31:0] out
);


  assign out = {value[27:24], value[31:28], value[19:16], value[23:20], value[11:8], value[15:12], value[3:0], value[7:4]};
endmodule

module u_ALU_rb8 (
  input  [31:0] value,
  output [31:0] out
);


  assign out = {value[23:16], value[31:24], value[7:0], value[15:8]};
endmodule

module u_ALU_rb16 (
  input  [31:0] value,
  output [31:0] out
);


  assign out = {value[15:0], value[31:16]};
endmodule

module u_DECODE (
  input  [31:0] instruction,
  output [4:0] RI_bits,
  output [4:0] RS_bits,
  output [4:0] RD_bits,
  output [2:0] JC,
  output [3:0] OP,
  output RI_or_imm,
  output RI_or_addr,
  output [23:0] addr,
  output [31:0] IMM
);

  // Probe on instruction[16:0]
  assign IMM = {{15{instruction[16]}}, instruction[16:0]};  // Bit_Extender bit_extender_1

  assign addr = instruction[23:0];
  assign JC = instruction[26:24];
  assign OP = instruction[31:28];
  assign RD_bits = instruction[26:22];
  assign RI_bits = instruction[4:0];
  assign RI_or_addr = instruction[27];
  assign RI_or_imm = instruction[27];
  assign RS_bits = instruction[21:17];

  // Other names for the same wires on the sheet: _0_4[4:0] = instruction[4:0]; _5_16[11:0] = instruction[16:5];
  //   _17_21[4:0] = instruction[21:17]; _22_23[1:0] = instruction[23:22]; _27 = instruction[27];
  //   _28_31[3:0] = instruction[31:28]; _24_26[2:0] = instruction[26:24]
endmodule

module u_jump_type (
  input  [2:0] JC,
  input  [31:0] JC_val,
  input  enable,
  output jump,
  output jal
);

  wire J, JAL_t, JC_Equals, JC_Greater, JC_Less, JEQ, JEQ_t, JGE, JGE_t, JGT, JGT_t, JLE, JLE_t, JLT, JLT_t,
       JNE, JNE_t, OR_2_out, OR_3_out, OR_4_out;

  Demultiplexer #(.select(3)) demultiplexer_1 (
    .out0(J), .out1(JGT), .out2(JEQ), .out3(JLT), .out4(JLE), .out5(JNE), .out6(JGE), .out7(JAL_t),
    .in(enable), .sel(JC));  // open: en
  Comparator #(.width(32), .mode("unsigned")) comparator_1 (
    .a(JC_val), .b({32{1'b0}}), .gt(JC_Greater), .eq(JC_Equals), .lt(JC_Less));
  or OR (jump, J, JGT_t, JEQ_t, JLT_t, JLE_t, JNE_t, JGE_t, JAL_t);
  and and_1 (jal, JAL_t, enable);
  or OR_2 (OR_2_out, JC_Equals, JC_Less);
  or OR_3 (OR_3_out, JC_Greater, JC_Less);
  or OR_4 (OR_4_out, JC_Greater, JC_Equals);
  and and_2 (JGT_t, enable, JGT, JC_Greater);
  and and_3 (JEQ_t, enable, JEQ, JC_Equals);
  and and_4 (JLT_t, enable, JLT, JC_Less);
  and and_5 (JLE_t, enable, JLE, OR_2_out);
  and and_6 (JNE_t, enable, JNE, OR_3_out);
  and and_7 (JGE_t, enable, JGE, OR_4_out);

  // Other names for the same wires on the sheet: jump_t = enable

  // Notes on the sheet:
  //   this will first return if jump condition is met or not
endmodule

module u_RD_write_enable (
  input  jump,
  input  jal,
  input  mem_write,
  output rd_write_enable
);

  wire and_2_out, and_3_out, JAL_jump, not_1_out, not_2_out, not_3_out, not_4_out;

  not not_1 (not_1_out, mem_write);
  not not_2 (not_2_out, jump);
  not not_3 (not_3_out, JAL_jump);
  not not_4 (not_4_out, mem_write);
  and and_1 (JAL_jump, jump, jal);
  and and_2 (and_2_out, jump, JAL_jump, not_1_out);
  and and_3 (and_3_out, not_2_out, not_3_out, not_4_out);
  or OR (rd_write_enable, and_2_out, and_3_out);
endmodule

module u_CONTROL (
  input  [2:0] JC,
  input  [3:0] OP,
  input  I_bit,
  input  [31:0] jc_value,
  output jumping,
  output RD_write,
  output mem,
  output mem_write,
  output word_mode,
  output JAL,
  output load
);

  wire demultiplexer_1_out10, demultiplexer_1_out11, demultiplexer_1_out12, demultiplexer_1_out13, J, JAL_t,
       JC_Equals, JC_Greater, JC_Less, JEQ, JEQ_t, JGE, JGE_t, JGT, JGT_t, JLE, JLE_t, JLT, JLT_t, JNE,
       JNE_t, jump, OR_6_out, OR_7_out, OR_8_out;

  Demultiplexer #(.select(4)) demultiplexer_1 (
    .out10(demultiplexer_1_out10), .out11(demultiplexer_1_out11), .out12(demultiplexer_1_out12),
    .out13(demultiplexer_1_out13), .out15(jump), .in(1'b1), .sel(OP));  // open: out0, out1, out2, out3, out4, out5, out6, out7, out8, out9, out14, en
  or OR (load, demultiplexer_1_out10, demultiplexer_1_out12);
  or OR_2 (mem_write, demultiplexer_1_out11, demultiplexer_1_out13);
  or OR_3 (word_mode, demultiplexer_1_out13, demultiplexer_1_out12);
  u_RD_write_enable u_RD_write (.jump(jump), .jal(JAL), .mem_write(mem_write), .rd_write_enable(RD_write));
  or OR_4 (mem, load, mem_write, word_mode);
  Demultiplexer #(.select(3)) demultiplexer_2 (
    .out0(J), .out1(JGT), .out2(JEQ), .out3(JLT), .out4(JLE), .out5(JNE), .out6(JGE), .out7(JAL_t),
    .in(jump), .sel(JC));  // open: en
  Comparator #(.width(32)) comparator_1 (.a(jc_value), .b({32{1'b0}}), .gt(JC_Greater), .eq(JC_Equals), .lt(JC_Less));
  or OR_5 (jumping, J, JGT_t, JEQ_t, JLT_t, JLE_t, JNE_t, JGE_t, JAL_t);
  and and_1 (JAL, JAL_t, jump);
  or OR_6 (OR_6_out, JC_Equals, JC_Less);
  or OR_7 (OR_7_out, JC_Greater, JC_Less);
  or OR_8 (OR_8_out, JC_Greater, JC_Equals);
  and and_2 (JGT_t, jump, JGT, JC_Greater);
  and and_3 (JEQ_t, jump, JEQ, JC_Equals);
  and and_4 (JLT_t, jump, JLT, JC_Less);
  and and_5 (JLE_t, jump, JLE, OR_6_out);
  and and_6 (JNE_t, jump, JNE, OR_7_out);
  and and_7 (JGE_t, jump, JGE, OR_8_out);

  // Other names for the same wires on the sheet: jc_val[31:0] = jc_value; jump_t = jumping;
  //   RD_write_enable = RD_write

  // Notes on the sheet:
  //   this will first return if jump condition is met or not
endmodule

module u_DIV (
  input  [31:0] rs_val,
  input  [31:0] val_2,
  output [31:0] out
);

  wire and_1_out, and_2_out, and_3_out, div_by_zero, equals, flip, greater, less;
  wire [31:0] adder_1_out, adder_2_out, multiplexer_1_out, multiplexer_4_out, multiplexer_5_out,
       negative_res, not_1_out, not_2_out, not_3_out, res, val_1_abs, val_2_abs;

  // Probe on rs_val
  // Probe on val_2
  assign not_1_out = ~rs_val;  // NOT_Gate not_1, 32 bits wide
  assign not_2_out = ~val_2;  // NOT_Gate not_2, 32 bits wide
  Adder #(.width(32)) adder_1 (.a(not_1_out), .b(32'h1), .out(adder_1_out));  // open: cin, cout
  Adder #(.width(32)) adder_2 (.a(not_2_out), .b(32'h1), .out(adder_2_out));  // open: cin, cout
  assign not_3_out = ~res;  // NOT_Gate not_3, 32 bits wide
  Adder #(.width(32)) adder_3 (.a(not_3_out), .b(32'h1), .out(negative_res));  // open: cin, cout
  Multiplexer #(.width(32)) multiplexer_1 (
    .in0(res), .in1(negative_res), .out(multiplexer_1_out), .sel(flip));  // open: en
  Multiplexer #(.width(32)) multiplexer_2 (
    .in0(rs_val), .in1(adder_1_out), .out(val_1_abs), .sel(rs_val[31]));  // open: en
  Multiplexer #(.width(32)) multiplexer_3 (
    .in0(val_2), .in1(adder_2_out), .out(val_2_abs), .sel(val_2[31]));  // open: en
  Divider #(.width(32)) divider_1 (.a(val_1_abs), .b(val_2_abs), .out(res));  // open: upper, rem
  Comparator #(.width(32)) comparator_1 (.a(val_2), .b({32{1'b0}}), .eq(div_by_zero));  // open: gt, lt
  Comparator #(.width(32)) comparator_2 (.a(rs_val), .b({32{1'b0}}), .gt(greater), .eq(equals), .lt(less));
  Multiplexer #(.width(32)) multiplexer_4 (
    .in0(multiplexer_1_out), .in1(32'h7fffffff), .out(multiplexer_4_out), .sel(and_1_out));  // open: en
  and and_1 (and_1_out, div_by_zero, greater);
  Multiplexer #(.width(32)) multiplexer_5 (
    .in0(multiplexer_4_out), .in1({32{1'b0}}), .out(multiplexer_5_out), .sel(and_2_out));  // open: en
  and and_2 (and_2_out, div_by_zero, equals);
  xor XOR (flip, rs_val[31], val_2[31]);
  Multiplexer #(.width(32)) multiplexer_6 (
    .in0(multiplexer_5_out), .in1(32'h80000000), .out(out), .sel(and_3_out));  // open: en
  and and_3 (and_3_out, div_by_zero, less);
  // Probe on out

  // Other names for the same wires on the sheet: output_val[31:0] = out; val_1[31:0] = rs_val
endmodule
